// Logisim project NetworkArchitecture.circ as structural Verilog
module main (
);

  wire A_0Write, A_1Write, A_2Write, A_3Write, A_4Write, A_5Write, A_6Write, A_7Write, B_0Write, B_1Write,
       CLEAR;
  wire [2:0] W_SLCT;
  wire [7:0] A_0E0, A_0E1, A_0E2, A_0E3, A_0E4, A_0E5, A_0E6, A_0E7, A_1E0, A_1E2, A_1E3, A_1E4, A_1E5,
       A_1E6, A_1E7, A_2E0, A_2E1, A_2E2, A_2E3, A_2E4, A_2E5, A_2E6, A_2E7, A_3E0, A_3E1, A_3E2, A_3E3,
       A_3E4, A_3E5, A_3E6, A_3E7, A_4E0, A_4E1, A_4E2, A_4E3, A_4E4, A_4E5, A_4E6, A_4E7, A_5E0, A_5E1,
       A_5E2, A_5E3, A_5E4, A_5E5, A_5E6, A_5E7, A_6E0, A_6E1, A_6E2, A_6E3, A_6E4, A_6E5, A_6E6, A_6E7,
       A_7E0, A_7E1, A_7E2, A_7E3, A_7E4, A_7E5, A_7E6, A_7E7, B_0E0, B_0E1, B_0E2, B_0E3, B_0E4, B_0E5,
       B_0E6, B_0E7, B_1E0, B_1E1, B_1E2, B_1E3, B_1E4, B_1E5, B_1E6, B_1E7, WGHT_IN;

  LinearNode linearnode_1 (
    .E0(A_0E0), .E1(A_0E1), .E2(A_0E2), .E3(A_0E3), .E4(A_0E4), .E5(A_0E5), .E6(A_0E6), .E7(A_0E7),
    .W_WRITE(A_0Write), .W_SLCT(W_SLCT), .W_IN(WGHT_IN), .CLEAR(CLEAR));  // open: IN_0, IN_1, IN_2, IN_3, IN_4, IN_5, IN_6, IN_7, CLK
  LinearNode linearnode_2 (
    .E0(A_1E0), .E1(A_0E1), .E2(A_1E2), .E3(A_1E3), .E4(A_1E4), .E5(A_1E5), .E6(A_1E6), .E7(A_1E7),
    .W_WRITE(A_1Write), .W_SLCT(W_SLCT), .W_IN(WGHT_IN), .CLEAR(CLEAR));  // open: IN_0, IN_1, IN_2, IN_3, IN_4, IN_5, IN_6, IN_7, CLK
  LinearNode linearnode_3 (
    .E0(A_2E0), .E1(A_2E1), .E2(A_2E2), .E3(A_2E3), .E4(A_2E4), .E5(A_2E5), .E6(A_2E6), .E7(A_2E7),
    .W_WRITE(A_2Write), .W_SLCT(W_SLCT), .W_IN(WGHT_IN), .CLEAR(CLEAR));  // open: IN_0, IN_1, IN_2, IN_3, IN_4, IN_5, IN_6, IN_7, CLK
  LinearNode linearnode_4 (
    .E0(A_3E0), .E1(A_3E1), .E2(A_3E2), .E3(A_3E3), .E4(A_3E4), .E5(A_3E5), .E6(A_3E6), .E7(A_3E7),
    .W_WRITE(A_3Write), .W_SLCT(W_SLCT), .W_IN(WGHT_IN), .CLEAR(CLEAR));  // open: IN_0, IN_1, IN_2, IN_3, IN_4, IN_5, IN_6, IN_7, CLK
  LinearNode linearnode_5 (
    .E0(A_4E0), .E1(A_4E1), .E2(A_4E2), .E3(A_4E3), .E4(A_4E4), .E5(A_4E5), .E6(A_4E6), .E7(A_4E7),
    .W_WRITE(A_4Write), .W_SLCT(W_SLCT), .W_IN(WGHT_IN), .CLEAR(CLEAR));  // open: IN_0, IN_1, IN_2, IN_3, IN_4, IN_5, IN_6, IN_7, CLK
  LinearNode linearnode_6 (
    .E0(A_5E0), .E1(A_5E1), .E2(A_5E2), .E3(A_5E3), .E4(A_5E4), .E5(A_5E5), .E6(A_5E6), .E7(A_5E7),
    .W_WRITE(A_5Write), .W_SLCT(W_SLCT), .W_IN(WGHT_IN), .CLEAR(CLEAR));  // open: IN_0, IN_1, IN_2, IN_3, IN_4, IN_5, IN_6, IN_7, CLK
  LinearNode linearnode_7 (
    .E0(A_6E0), .E1(A_6E1), .E2(A_6E2), .E3(A_6E3), .E4(A_6E4), .E5(A_6E5), .E6(A_6E6), .E7(A_6E7),
    .W_WRITE(A_6Write), .W_SLCT(W_SLCT), .W_IN(WGHT_IN), .CLEAR(CLEAR));  // open: IN_0, IN_1, IN_2, IN_3, IN_4, IN_5, IN_6, IN_7, CLK
  LinearNode linearnode_8 (
    .E0(A_7E0), .E1(A_7E1), .E2(A_7E2), .E3(A_7E3), .E4(A_7E4), .E5(A_7E5), .E6(A_7E6), .E7(A_7E7),
    .W_WRITE(A_7Write), .W_SLCT(W_SLCT), .W_IN(WGHT_IN), .CLEAR(CLEAR));  // open: IN_0, IN_1, IN_2, IN_3, IN_4, IN_5, IN_6, IN_7, CLK
  LinearNode linearnode_9 (
    .IN_0(A_0E0), .IN_1(A_1E0), .IN_2(A_2E0), .IN_3(A_3E0), .IN_4(A_4E0), .IN_5(A_5E0), .IN_6(A_6E0),
    .IN_7(A_7E0), .E0(B_0E0), .E1(B_0E1), .E2(B_0E2), .E3(B_0E3), .E4(B_0E4), .E5(B_0E5), .E6(B_0E6),
    .E7(B_0E7), .W_WRITE(B_0Write), .W_SLCT(W_SLCT), .W_IN(WGHT_IN), .CLEAR(CLEAR));  // open: CLK
  LinearNode linearnode_10 (
    .IN_0(A_0E1), .IN_1(A_0E1), .IN_2(A_2E1), .IN_3(A_3E1), .IN_4(A_4E1), .IN_5(A_5E1), .IN_6(A_6E1),
    .IN_7(A_7E1), .E0(B_1E0), .E1(B_1E1), .E2(B_1E2), .E3(B_1E3), .E4(B_1E4), .E5(B_1E5), .E6(B_1E6),
    .E7(B_1E7), .W_WRITE(B_1Write), .W_SLCT(W_SLCT), .W_IN(WGHT_IN), .CLEAR(CLEAR));  // open: CLK
  LinearNode linearnode_11 (
    .IN_0(A_0E2), .IN_1(A_1E2), .IN_2(A_2E2), .IN_3(A_3E2), .IN_4(A_4E2), .IN_5(A_5E2), .IN_6(A_6E2),
    .IN_7(A_7E2), .E0(A_2E0), .E1(A_2E1), .E2(A_2E2), .E3(A_2E3), .E4(A_2E4), .E5(A_2E5), .E6(A_2E6),
    .E7(A_2E7), .W_WRITE(A_2Write), .W_SLCT(W_SLCT), .W_IN(WGHT_IN), .CLEAR(CLEAR));  // open: CLK
  LinearNode linearnode_12 (
    .IN_0(A_0E3), .IN_1(A_1E3), .IN_2(A_2E3), .IN_3(A_3E3), .IN_4(A_4E3), .IN_5(A_5E3), .IN_6(A_6E3),
    .IN_7(A_7E3), .E0(A_3E0), .E1(A_3E1), .E2(A_3E2), .E3(A_3E3), .E4(A_3E4), .E5(A_3E5), .E6(A_3E6),
    .E7(A_3E7), .W_WRITE(A_3Write), .W_SLCT(W_SLCT), .W_IN(WGHT_IN), .CLEAR(CLEAR));  // open: CLK
  LinearNode linearnode_13 (
    .IN_0(A_0E4), .IN_1(A_1E4), .IN_2(A_2E4), .IN_3(A_3E4), .IN_4(A_4E4), .IN_5(A_5E4), .IN_6(A_6E4),
    .IN_7(A_7E4), .E0(A_4E0), .E1(A_4E1), .E2(A_4E2), .E3(A_4E3), .E4(A_4E4), .E5(A_4E5), .E6(A_4E6),
    .E7(A_4E7), .W_WRITE(A_4Write), .W_SLCT(W_SLCT), .W_IN(WGHT_IN), .CLEAR(CLEAR));  // open: CLK
  LinearNode linearnode_14 (
    .IN_0(A_0E5), .IN_1(A_1E5), .IN_2(A_2E5), .IN_3(A_3E5), .IN_4(A_4E5), .IN_5(A_5E5), .IN_6(A_6E5),
    .IN_7(A_7E5), .E0(A_5E0), .E1(A_5E1), .E2(A_5E2), .E3(A_5E3), .E4(A_5E4), .E5(A_5E5), .E6(A_5E6),
    .E7(A_5E7), .W_WRITE(A_5Write), .W_SLCT(W_SLCT), .W_IN(WGHT_IN), .CLEAR(CLEAR));  // open: CLK
  LinearNode linearnode_15 (
    .IN_0(A_0E6), .IN_1(A_1E6), .IN_2(A_2E6), .IN_3(A_3E6), .IN_4(A_4E6), .IN_5(A_5E6), .IN_6(A_6E6),
    .IN_7(A_7E6), .E0(A_6E0), .E1(A_6E1), .E2(A_6E2), .E3(A_6E3), .E4(A_6E4), .E5(A_6E5), .E6(A_6E6),
    .E7(A_6E7), .W_WRITE(A_6Write), .W_SLCT(W_SLCT), .W_IN(WGHT_IN), .CLEAR(CLEAR));  // open: CLK
  LinearNode linearnode_16 (
    .IN_0(A_0E7), .IN_1(A_1E7), .IN_2(A_2E7), .IN_3(A_3E7), .IN_4(A_4E7), .IN_5(A_5E7), .IN_6(A_6E7),
    .IN_7(A_7E7), .E0(A_7E0), .E1(A_7E1), .E2(A_7E2), .E3(A_7E3), .E4(A_7E4), .E5(A_7E5), .E6(A_7E6),
    .E7(A_7E7), .W_WRITE(A_7Write), .W_SLCT(W_SLCT), .W_IN(WGHT_IN), .CLEAR(CLEAR));  // open: CLK

  // Other names for the same wires on the sheet: A_1E1[7:0] = A_0E1
endmodule

module LinearNode (
  input  [7:0] IN_0,
  input  [7:0] E0,
  input  [7:0] IN_1,
  input  [7:0] E1,
  input  [7:0] IN_2,
  input  [7:0] E2,
  input  [7:0] IN_3,
  input  [7:0] E3,
  input  [7:0] IN_4,
  input  [7:0] E4,
  input  [7:0] IN_5,
  input  [7:0] E5,
  input  [7:0] IN_6,
  input  [7:0] E6,
  input  [7:0] IN_7,
  input  [7:0] E7,
  input  W_WRITE,
  input  [2:0] W_SLCT,
  input  [7:0] W_IN,
  input  CLEAR,
  input  CLK
);

  wire decoder_1_out0, decoder_1_out1, decoder_1_out2, decoder_1_out3, decoder_1_out4, decoder_1_out5,
       decoder_1_out6, decoder_1_out7, W0_Write, W1_Write, W2_Write, W3_Write, W4_Write, W5_Write, W6_Write,
       W7_Write;
  wire [7:0] adder_1_out, adder_2_out, adder_3_out, adder_4_out, adder_5_out, adder_6_out, adder_7_out, BIAS,
       FUNC_OUT, multiplier_1_out, multiplier_2_out, multiplier_3_out, multiplier_4_out, multiplier_5_out,
       multiplier_6_out, multiplier_7_out, multiplier_8_out, W0, W1, W2, W3, W4, W5, W6, W7;

  Decoder #(.select(3), .disabled(0), .enable("false")) decoder_1 (
    .out0(decoder_1_out0), .out1(decoder_1_out1), .out2(decoder_1_out2), .out3(decoder_1_out3),
    .out4(decoder_1_out4), .out5(decoder_1_out5), .out6(decoder_1_out6), .out7(decoder_1_out7), .sel(W_SLCT));
  Adder adder_1 (.a(IN_0), .b(IN_1), .out(adder_1_out), .cin(1'b0));  // open: cout
  Adder adder_2 (.a(IN_2), .b(IN_3), .out(adder_2_out), .cin(1'b0));  // open: cout
  Adder adder_3 (.a(IN_4), .b(IN_5), .out(adder_3_out), .cin(1'b0));  // open: cout
  Adder adder_4 (.a(IN_6), .b(IN_7), .out(adder_4_out), .cin(1'b0));  // open: cout
  and and_1 (W0_Write, decoder_1_out0, W_WRITE);
  and and_2 (W1_Write, decoder_1_out1, W_WRITE);
  and and_3 (W2_Write, decoder_1_out2, W_WRITE);
  and and_4 (W3_Write, decoder_1_out3, W_WRITE);
  and and_5 (W4_Write, decoder_1_out4, W_WRITE);
  and and_6 (W5_Write, decoder_1_out5, W_WRITE);
  and and_7 (W6_Write, decoder_1_out6, W_WRITE);
  and and_8 (W7_Write, decoder_1_out7, W_WRITE);
  Adder adder_5 (.a(adder_1_out), .b(adder_2_out), .out(adder_5_out), .cin(1'b0));  // open: cout
  Adder adder_6 (.a(adder_3_out), .b(adder_4_out), .out(adder_6_out), .cin(1'b0));  // open: cout
  Adder adder_7 (.a(adder_5_out), .b(adder_6_out), .out(adder_7_out), .cin(1'b0));  // open: cout
  Adder adder_8 (.a(adder_7_out), .b(BIAS), .out(FUNC_OUT), .cin(1'b0));  // open: cout
  Register #(.trigger("high")) register_1 (.D(W_IN), .en(1'b1), .Q(W0), .clk(W0_Write), .clr(CLEAR));
  Register #(.trigger("high")) register_2 (.D(W_IN), .en(1'b1), .Q(W1), .clk(W1_Write), .clr(CLEAR));
  Register #(.trigger("high")) register_3 (.D(W_IN), .en(1'b1), .Q(W2), .clk(W2_Write), .clr(CLEAR));
  Register #(.trigger("high")) register_4 (.D(W_IN), .en(1'b1), .Q(W3), .clk(W3_Write), .clr(CLEAR));
  Register #(.trigger("high")) register_5 (.D(W_IN), .en(1'b1), .Q(W4), .clk(W4_Write), .clr(CLEAR));
  Register #(.trigger("high")) register_6 (.D(W_IN), .en(1'b1), .Q(W5), .clk(W5_Write), .clr(CLEAR));
  Register #(.trigger("high")) register_7 (.D(W_IN), .en(1'b1), .Q(W6), .clk(W6_Write), .clr(CLEAR));
  Register #(.trigger("high")) register_8 (.D(W_IN), .en(1'b1), .Q(W7), .clk(W7_Write), .clr(CLEAR));
  Multiplier multiplier_1 (.a(FUNC_OUT), .b(W0), .out(multiplier_1_out), .cin({8{1'b0}}));  // open: cout
  Multiplier multiplier_2 (.a(FUNC_OUT), .b(W1), .out(multiplier_2_out), .cin({8{1'b0}}));  // open: cout
  Multiplier multiplier_3 (.a(FUNC_OUT), .b(W2), .out(multiplier_3_out), .cin({8{1'b0}}));  // open: cout
  Multiplier multiplier_4 (.a(FUNC_OUT), .b(W3), .out(multiplier_4_out), .cin({8{1'b0}}));  // open: cout
  Multiplier multiplier_5 (.a(FUNC_OUT), .b(W4), .out(multiplier_5_out), .cin({8{1'b0}}));  // open: cout
  Multiplier multiplier_6 (.a(FUNC_OUT), .b(W5), .out(multiplier_6_out), .cin({8{1'b0}}));  // open: cout
  Multiplier multiplier_7 (.a(FUNC_OUT), .b(W6), .out(multiplier_7_out), .cin({8{1'b0}}));  // open: cout
  Multiplier multiplier_8 (.a(FUNC_OUT), .b(W7), .out(multiplier_8_out), .cin({8{1'b0}}));  // open: cout
  Register #(.trigger("high")) register_9 (.D(multiplier_1_out), .en(1'b1), .Q(E0), .clk(CLK), .clr(CLEAR));
  Register #(.trigger("high")) register_10 (.D(multiplier_2_out), .en(1'b1), .Q(E1), .clk(CLK), .clr(CLEAR));
  Register #(.trigger("high")) register_11 (.D(multiplier_3_out), .en(1'b1), .Q(E2), .clk(CLK), .clr(CLEAR));
  Register #(.trigger("high")) register_12 (.D(multiplier_4_out), .en(1'b1), .Q(E3), .clk(CLK), .clr(CLEAR));
  Register #(.trigger("high")) register_13 (.D(multiplier_5_out), .en(1'b1), .Q(E4), .clk(CLK), .clr(CLEAR));
  Register #(.trigger("high")) register_14 (.D(multiplier_6_out), .en(1'b1), .Q(E5), .clk(CLK), .clr(CLEAR));
  Register #(.trigger("high")) register_15 (.D(multiplier_7_out), .en(1'b1), .Q(E6), .clk(CLK), .clr(CLEAR));
  Register #(.trigger("high")) register_16 (.D(multiplier_8_out), .en(1'b1), .Q(E7), .clk(CLK), .clr(CLEAR));

  // Other names for the same wires on the sheet: E0_OUT[7:0] = E0; E1_OUT[7:0] = E1; E2_OUT[7:0] = E2;
  //   E3_OUT[7:0] = E3; E4_OUT[7:0] = E4; E5_OUT[7:0] = E5; E6_OUT[7:0] = E6; E7_OUT[7:0] = E7;
  //   W_SELECT[2:0] = W_SLCT

  // Notes on the sheet:
  //   Linear Addition
  //   Weight Writing/Storage
  //   Weight Multiplication
  //   Input
  //   Output
endmodule

module LinearNode_Bus (
  input  [7:0] IN,
  input  FUNC_CLEAR,
  input  EVALUATE,
  input  W_WRITE,
  input  [2:0] W_SLCT,
  input  [7:0] W_IN,
  input  CLEAR,
  input  CLK,
  output [7:0] E0,
  output [7:0] E1,
  output [7:0] E2,
  output [7:0] E3,
  output [7:0] E4,
  output [7:0] E5,
  output [7:0] E6,
  output [7:0] E7
);

  wire decoder_1_out0, decoder_1_out1, decoder_1_out2, decoder_1_out3, decoder_1_out4, decoder_1_out5,
       decoder_1_out6, decoder_1_out7, not_1_out, W0_Write, W1_Write, W2_Write, W3_Write, W4_Write, W5_Write,
       W6_Write, W7_Write;
  wire [7:0] adder_1_out, FUNC_OUT, multiplier_1_out, multiplier_2_out, multiplier_3_out, multiplier_4_out,
       multiplier_5_out, multiplier_6_out, multiplier_7_out, multiplier_8_out, register_1_q, W0, W1, W2, W3,
       W4, W5, W6, W7;

  Decoder #(.select(3), .disabled(0), .enable("false")) decoder_1 (
    .out0(decoder_1_out0), .out1(decoder_1_out1), .out2(decoder_1_out2), .out3(decoder_1_out3),
    .out4(decoder_1_out4), .out5(decoder_1_out5), .out6(decoder_1_out6), .out7(decoder_1_out7), .sel(W_SLCT));
  not not_1 (not_1_out, EVALUATE);
  Adder adder_1 (.a(IN), .b(register_1_q), .out(adder_1_out), .cin(1'b0));  // open: cout
  and and_1 (W0_Write, decoder_1_out0, W_WRITE);
  and and_2 (W1_Write, decoder_1_out1, W_WRITE);
  and and_3 (W2_Write, decoder_1_out2, W_WRITE);
  and and_4 (W3_Write, decoder_1_out3, W_WRITE);
  and and_5 (W4_Write, decoder_1_out4, W_WRITE);
  and and_6 (W5_Write, decoder_1_out5, W_WRITE);
  and and_7 (W6_Write, decoder_1_out6, W_WRITE);
  and and_8 (W7_Write, decoder_1_out7, W_WRITE);
  Register register_1 (.D(adder_1_out), .en(not_1_out), .Q(register_1_q), .clk(CLK), .clr(FUNC_CLEAR));
  // Transmission_Gate #(.gate("br"), .width(8)) transmission_1: pin names not known; wires that end beside it: register_1_q, EVALUATE, not_1_out, FUNC_OUT
  Transistor #(.\type ("n"), .width(8)) transistor_1 (.in({8{1'b0}}), .out(FUNC_OUT), .gate(not_1_out));
  Register #(.trigger("high")) register_2 (.D(W_IN), .en(1'b1), .Q(W0), .clk(W0_Write), .clr(CLEAR));
  Register #(.trigger("high")) register_3 (.D(W_IN), .en(1'b1), .Q(W1), .clk(W1_Write), .clr(CLEAR));
  Register #(.trigger("high")) register_4 (.D(W_IN), .en(1'b1), .Q(W2), .clk(W2_Write), .clr(CLEAR));
  Register #(.trigger("high")) register_5 (.D(W_IN), .en(1'b1), .Q(W3), .clk(W3_Write), .clr(CLEAR));
  Register #(.trigger("high")) register_6 (.D(W_IN), .en(1'b1), .Q(W4), .clk(W4_Write), .clr(CLEAR));
  Register #(.trigger("high")) register_7 (.D(W_IN), .en(1'b1), .Q(W5), .clk(W5_Write), .clr(CLEAR));
  Register #(.trigger("high")) register_8 (.D(W_IN), .en(1'b1), .Q(W6), .clk(W6_Write), .clr(CLEAR));
  Register #(.trigger("high")) register_9 (.D(W_IN), .en(1'b1), .Q(W7), .clk(W7_Write), .clr(CLEAR));
  Multiplier multiplier_1 (.a(FUNC_OUT), .b(W0), .out(multiplier_1_out), .cin({8{1'b0}}));  // open: cout
  Multiplier multiplier_2 (.a(FUNC_OUT), .b(W1), .out(multiplier_2_out), .cin({8{1'b0}}));  // open: cout
  Multiplier multiplier_3 (.a(FUNC_OUT), .b(W2), .out(multiplier_3_out), .cin({8{1'b0}}));  // open: cout
  Multiplier multiplier_4 (.a(FUNC_OUT), .b(W3), .out(multiplier_4_out), .cin({8{1'b0}}));  // open: cout
  Multiplier multiplier_5 (.a(FUNC_OUT), .b(W4), .out(multiplier_5_out), .cin({8{1'b0}}));  // open: cout
  Multiplier multiplier_6 (.a(FUNC_OUT), .b(W5), .out(multiplier_6_out), .cin({8{1'b0}}));  // open: cout
  Multiplier multiplier_7 (.a(FUNC_OUT), .b(W6), .out(multiplier_7_out), .cin({8{1'b0}}));  // open: cout
  Multiplier multiplier_8 (.a(FUNC_OUT), .b(W7), .out(multiplier_8_out), .cin({8{1'b0}}));  // open: cout
  Register #(.trigger("high")) register_10 (.D(multiplier_1_out), .en(1'b1), .Q(E0), .clk(EVALUATE), .clr(CLEAR));
  Register #(.trigger("high")) register_11 (.D(multiplier_2_out), .en(1'b1), .Q(E1), .clk(EVALUATE), .clr(CLEAR));
  Register #(.trigger("high")) register_12 (.D(multiplier_3_out), .en(1'b1), .Q(E2), .clk(EVALUATE), .clr(CLEAR));
  Register #(.trigger("high")) register_13 (.D(multiplier_4_out), .en(1'b1), .Q(E3), .clk(EVALUATE), .clr(CLEAR));
  Register #(.trigger("high")) register_14 (.D(multiplier_5_out), .en(1'b1), .Q(E4), .clk(EVALUATE), .clr(CLEAR));
  Register #(.trigger("high")) register_15 (.D(multiplier_6_out), .en(1'b1), .Q(E5), .clk(EVALUATE), .clr(CLEAR));
  Register #(.trigger("high")) register_16 (.D(multiplier_7_out), .en(1'b1), .Q(E6), .clk(EVALUATE), .clr(CLEAR));
  Register #(.trigger("high")) register_17 (.D(multiplier_8_out), .en(1'b1), .Q(E7), .clk(EVALUATE), .clr(CLEAR));

  // Other names for the same wires on the sheet: E0_OUT[7:0] = E0; E1_OUT[7:0] = E1; E2_OUT[7:0] = E2;
  //   E3_OUT[7:0] = E3; E4_OUT[7:0] = E4; E5_OUT[7:0] = E5; E6_OUT[7:0] = E6; E7_OUT[7:0] = E7;
  //   W_SELECT[2:0] = W_SLCT

  // Notes on the sheet:
  //   Linear Addition
  //   Weight Writing/Storage
  //   Weight Multiplication
  //   Input
  //   Output
endmodule
